// Logisim project 4 bit Adder.circ as structural Verilog: 1 circuit, main circuit main
// Adder
module main (
  input  A0,
  input  B0,
  input  A1,
  input  B1,
  input  A2,
  input  B2,
  input  A3,
  input  B3,
  output Sum0,
  output Sum1,
  output Sum2,
  output Sum3,
  output Carry
);

  wire and_1_out, and_2_out, and_3_out, and_4_out, and_5_out, and_6_out, and_7_out, and_8_out, or_1_out,
       or_2_out, or_3_out, xor_1_out, xor_2_out, xor_5_out, xor_6_out;

  xor xor_1 (xor_1_out, A0, B0);
  and and_1 (and_1_out, A0, B0);
  xor xor_2 (xor_2_out, A2, B2);
  and and_2 (and_2_out, A2, B2);
  xor xor_3 (Sum0, 1'b0, xor_1_out);
  and and_3 (and_3_out, 1'b0, xor_1_out);
  xor xor_4 (Sum2, or_3_out, xor_2_out);
  and and_4 (and_4_out, or_3_out, xor_2_out);
  or or_1 (or_1_out, and_3_out, and_1_out);
  or or_2 (or_2_out, and_4_out, and_2_out);
  xor xor_5 (xor_5_out, A1, B1);
  and and_5 (and_5_out, A1, B1);
  xor xor_6 (xor_6_out, A3, B3);
  and and_6 (and_6_out, A3, B3);
  xor xor_7 (Sum1, or_1_out, xor_5_out);
  and and_7 (and_7_out, or_1_out, xor_5_out);
  xor xor_8 (Sum3, or_2_out, xor_6_out);
  and and_8 (and_8_out, or_2_out, xor_6_out);
  or or_3 (or_3_out, and_7_out, and_5_out);
  or or_4 (Carry, and_8_out, and_6_out);

  // Notes on the sheet:
  //   B Input
  //   A Input
  //   V
  //   V
  //   4 bit Adder
endmodule
