// Logisim project 4BitAdderSub.circ as structural Verilog: 1 circuit, main circuit main
module main (
  input  A4,
  input  A3,
  input  A2,
  input  A1,
  input  B4,
  input  B3,
  input  B2,
  input  B1,
  output Overflow,
  output Sum4,
  output Sum3,
  output Sum2,
  output Sum1
);

  wire main_2_carry, main_3_carry, main_4_carry, undriven, undriven_2, undriven_3, undriven_4, undriven_5;

  FullAdder2_main main_1 (.Carry_in(main_2_carry), .A_in(A4), .B_in(B4), .Sum(Sum4), .Carry(Overflow));
  // XOR_Gate xor_1 has open pins: in0=undriven, in1=undriven_2, out=open
  FullAdder2_main main_2 (.Carry_in(main_3_carry), .A_in(A3), .B_in(B3), .Sum(Sum3), .Carry(main_2_carry));
  // XOR_Gate xor_2 has open pins: in0=undriven, in1=undriven_3, out=open
  FullAdder2_main main_3 (.Carry_in(main_4_carry), .A_in(A2), .B_in(B2), .Sum(Sum2), .Carry(main_3_carry));
  // XOR_Gate xor_3 has open pins: in0=undriven, in1=undriven_4, out=open
  FullAdder2_main main_4 (.Carry_in(1'b0), .A_in(A1), .B_in(B1), .Sum(Sum1), .Carry(main_4_carry));
  // XOR_Gate xor_4 has open pins: in0=undriven, in1=undriven_5, out=open
endmodule
